// Logisim project processor.circ as structural Verilog: 13 circuits, main circuit MIPS32
module MIPS32 (
);

  wire clock_1_out, loadusehazard_1_hazard, loadusehazard_2_hazard, not_1_out, or_1_out;
  wire [4:0] rs, rt;
  wire [31:0] A_q, B_2_q, B_q, ctrl_2_q, ctrl_3_q, ctrl_id_o, ctrl_q, ctrl_wb_o, D_2_q, D_q, ex_1_bout,
       ex_1_ctrlout, ex_1_d, forwarder_1_correctdata, forwarder_2_correctdata, id_1_a, id_1_b, id_1_imm,
       id_1_pc_4out, if_1_inst, if_1_pc_4, imm_q, ins_q, M_q, mem_1_ctrlout, mem_1_dout, mem_1_m, PC_4_2_q,
       PC_4_q, target, wb;
  wire [31:31] and_1_out;

  IF if_1 (
    .Clock(clock_1_out), .target(target), .ctrl(ctrl_id_o), .NOP(and_1_out[31]), .inst(if_1_inst),
    .PC_4(if_1_pc_4));
  Register #(.width(32)) ins (
    .D(if_1_inst), .Q({ins_q[31:16], rt, rs, ins_q[5:0]}), .clk(clock_1_out));  // open: en, clr
  Register #(.width(32)) PC_4 (.D(if_1_pc_4), .Q(PC_4_q), .clk(clock_1_out));  // open: en, clr
  and and_1 (and_1_out[31], not_1_out, ctrl_id_o[5], or_1_out);
  not not_1 (not_1_out, ctrl_id_o[6]);
  or or_1 (or_1_out, loadusehazard_1_hazard, loadusehazard_2_hazard);
  ID id_1 (
    .ctrl(ctrl_wb_o), .inst({ins_q[31:16], rt, rs, ins_q[5:0]}), .PC_4(PC_4_q), .A(id_1_a), .B(id_1_b),
    .imm(id_1_imm), .PC_4out(id_1_pc_4out), .ctrl_2(ctrl_id_o), .wb(wb), .Clock(clock_1_out), .target(target));
  LoadUseHazard loadusehazard_1 (.InputRegister(rs), .ctrl(ctrl_q), .Hazard(loadusehazard_1_hazard));
  LoadUseHazard loadusehazard_2 (.InputRegister(rt), .ctrl(ctrl_q), .Hazard(loadusehazard_2_hazard));
  Forwarder forwarder_1 (
    .InputData(id_1_a), .InputReg(rs), .ForwardEX(ex_1_d), .ForwardMEM(mem_1_dout),
    .ctrl_ex_out(ex_1_ctrlout), .ctrl_mem_out(ctrl_3_q), .CorrectData(forwarder_1_correctdata));
  Register #(.width(32)) A (.D(forwarder_1_correctdata), .Q(A_q), .clk(clock_1_out), .clr(clock_1_out));  // open: en
  Register #(.width(32)) B (.D(forwarder_2_correctdata), .Q(B_q), .clk(clock_1_out));  // open: en, clr
  Forwarder forwarder_2 (
    .InputData(id_1_b), .InputReg(rt), .ForwardEX(ex_1_d), .ForwardMEM(mem_1_dout),
    .ctrl_ex_out(ex_1_ctrlout), .ctrl_mem_out(ctrl_3_q), .CorrectData(forwarder_2_correctdata));
  Register #(.width(32)) imm (.D(id_1_imm), .Q(imm_q), .clk(clock_1_out));  // open: en, clr
  Register #(.width(32)) PC_4_2 (.D(id_1_pc_4out), .Q(PC_4_2_q), .clk(clock_1_out));  // open: en, clr
  Register #(.width(32)) ctrl (.D({and_1_out[31], ctrl_id_o[30:0]}), .Q(ctrl_q), .clk(clock_1_out));  // open: en, clr
  EX ex_1 (
    .A(A_q), .B(B_q), .imm(imm_q), .PC_4(PC_4_2_q), .ctrl(ctrl_q), .D(ex_1_d), .Bout(ex_1_bout),
    .ctrlout(ex_1_ctrlout));  // open: target
  Register #(.width(32)) D (.D(ex_1_d), .Q(D_q), .clk(clock_1_out));  // open: en, clr
  Register #(.width(32)) B_2 (.D(ex_1_bout), .Q(B_2_q), .clk(clock_1_out));  // open: en, clr
  Register #(.width(32)) ctrl_2 (.D(ex_1_ctrlout), .Q(ctrl_2_q), .clk(clock_1_out));  // open: en, clr
  Register #(.width(32)) D_2 (.D(mem_1_dout), .Q(D_2_q), .clk(clock_1_out));  // open: en, clr
  MEM mem_1 (
    .D(D_q), .B(B_2_q), .ctrl(ctrl_2_q), .Clock(clock_1_out), .Dout(mem_1_dout), .M(mem_1_m),
    .ctrlout(mem_1_ctrlout));
  Register #(.width(32)) M (.D(mem_1_m), .Q(M_q), .clk(clock_1_out));  // open: en, clr
  Register #(.width(32)) ctrl_3 (.D(mem_1_ctrlout), .Q(ctrl_3_q), .clk(clock_1_out));  // open: en, clr
  Clock clock_1 (.out(clock_1_out));
  WB wb_1 (.D(D_2_q), .M(M_q), .ctrl(ctrl_3_q), .WB(wb), .ctrl_out(ctrl_wb_o));
endmodule

module EX (
  input  [31:0] A,
  input  [31:0] B,
  input  [31:0] imm,
  input  [31:0] PC_4,
  input  [31:0] ctrl,
  output [31:0] target,
  output [31:0] D,
  output [31:0] Bout,
  output [31:0] ctrlout
);

  wire [4:0] multiplexer_2_out;
  wire [31:0] mips_alu_1_p5, multiplexer_1_out, our_alu_1_d;

  Multiplexer #(.width(32), .enable("false")) multiplexer_1 (.in0(B), .in1(imm), .out(multiplexer_1_out));  // open: sel
  Multiplexer #(.width(5)) multiplexer_2 (
    .in0(A[4:0]), .in1(ctrl[23:19]), .out(multiplexer_2_out), .sel(ctrl[9]));  // open: en
  // Mips_ALU mips_alu_1: pin names not known; wires that end beside it: A, multiplexer_1_out, ctrl[4:1], multiplexer_2_out, mips_alu_1_p5, PC_4, target
  Our_ALU our_alu_1 (.A(A), .B(multiplexer_1_out), .op(ctrl[4:1]), .D(our_alu_1_d));
  Multiplexer #(.width(32)) multiplexer_3 (.in0(mips_alu_1_p5), .in1(our_alu_1_d), .out(D), .sel(ctrl[0]));  // open: en

  assign Bout = B;
  assign ctrlout = ctrl;

  // Other names for the same wires on the sheet: UseALU = ctrl[0]; Lower5Bit[4:0] = A[4:0]; opcode[3:0] = ctrl[4:1];
  //   shamt[4:0] = ctrl[23:19]
endmodule

module IF (
  input  [31:0] ctrl,
  input  [31:0] target,
  input  Clock,
  input  NOP,
  output [31:0] inst,
  output [31:0] PC_4
);

  wire not_1_out;
  wire [31:0] multiplexer_1_out, register_1_q;

  Multiplexer #(.width(32), .enable("false")) multiplexer_1 (
    .in0(PC_4), .in1(target), .out(multiplexer_1_out), .sel(ctrl[7]));
  Add4 add4_1 (.In(register_1_q), .Out(PC_4));
  Register #(.width(32)) register_1 (
    .D(multiplexer_1_out), .en(not_1_out), .Q(register_1_q), .clk(Clock));  // open: clr
  not not_1 (not_1_out, NOP);
  // MIPSProgramROM mipsprogramrom_1: pin names not known; wires that end beside it: register_1_q, inst

  // Other names for the same wires on the sheet: tPC_4[31:0] = PC_4
endmodule

module MEM (
  input  [31:0] D,
  input  [31:0] B,
  input  [31:0] ctrl,
  input  Clock,
  output [31:0] Dout,
  output [31:0] M,
  output [31:0] ctrlout
);

  // MIPS_RAM mips_ram_1: pin names not known; wires that end beside it: D[23:0], B, ctrl[11], Clock, ctrl[10], M

  assign ctrlout = ctrl;
  assign Dout = D;
endmodule

module WB (
  input  [31:0] D,
  input  [31:0] M,
  input  [31:0] ctrl,
  output [31:0] WB,
  output [31:0] ctrl_out
);

  Multiplexer #(.width(32), .enable("false")) multiplexer_1 (.in0(D), .in1(M), .out(WB), .sel(ctrl[10]));

  assign ctrl_out = ctrl;
endmodule

module ID (
  input  [31:0] ctrl,
  input  [31:0] wb,
  input  [31:0] inst,
  input  [31:0] PC_4,
  input  Clock,
  output [31:0] A,
  output [31:0] B,
  output [31:0] imm,
  output [31:0] PC_4out,
  output [31:0] ctrl_2,
  output [31:0] target
);

  wire and_1_out, and_2_out, BranchIn, comparator_1_gt, comparator_1_lt, comparator_2_eq, comparator_3_eq,
       multiplexer_1_out, multiplexer_2_out, not_1_out, undriven, WBIn, xor_1_out, xor_2_out;
  wire [4:0] decoder_1_rs, decoder_1_rt;
  wire [15:0] imm16;
  wire [31:0] A_t, adder_1_out, bit_extender_1_out, bit_extender_2_out, decoder_1_target, plus_4_out;

  Comparator #(.width(32)) comparator_1 (
    .a(A_t), .b({32{1'b0}}), .gt(comparator_1_gt), .lt(comparator_1_lt));  // open: eq
  Comparator #(.width(32)) comparator_2 (.a(B), .b({32{1'b0}}), .eq(comparator_2_eq));  // open: gt, lt
  Comparator #(.width(32)) comparator_3 (.a(A_t), .b(B), .eq(comparator_3_eq));  // open: gt, lt
  Multiplexer #(.enable("false")) multiplexer_1 (
    .in0(comparator_1_gt), .in1(comparator_1_lt), .out(multiplexer_1_out));  // open: sel
  not not_1 (not_1_out, comparator_2_eq);
  xor xor_1 (xor_1_out, comparator_3_eq, undriven);
  xor xor_2 (xor_2_out, undriven, multiplexer_1_out);
  Multiplexer multiplexer_2 (
    .in0(comparator_2_eq), .in1(not_1_out), .out(multiplexer_2_out), .sel(ctrl_2[1]));  // open: en
  Multiplexer multiplexer_3 (.in0(xor_1_out), .in1(xor_2_out));  // open: out, sel, en
  buf and_1 (and_1_out, BranchIn);  // AND_Gate
  and and_2 (and_2_out, multiplexer_2_out, ctrl_2[14]);
  Decoder decoder_1 (
    .ins(inst), .PC_4(PC_4), .rs(decoder_1_rs), .rt(decoder_1_rt), .imm(imm16),
    .ctrl({ctrl_2[31:9], WBIn, BranchIn, ctrl_2[6:0]}), .target(decoder_1_target));
  or or_1 (ctrl_2[7], and_1_out, ctrl_2[6]);
  or or_2 (ctrl_2[8], and_2_out, WBIn);
  // RegisterFile registerfile_1: pin names not known; wires that end beside it: wb, Clock, ctrl[8], ctrl[19:15], decoder_1_rs, decoder_1_rt, A_t, B
  assign bit_extender_1_out = {{16{1'b0}}, imm16};  // Bit_Extender bit_extender_1
  assign bit_extender_2_out = {{16{imm16[15]}}, imm16};  // Bit_Extender bit_extender_2
  Multiplexer #(.width(32), .enable("false")) multiplexer_4 (
    .in0(bit_extender_1_out), .in1(bit_extender_2_out), .out(imm), .sel(ctrl_2[13]));
  Adder #(.width(32)) adder_1 (
    .a(PC_4), .b({{15{imm16[15]}}, imm16[14:0], 2'b00}), .out(adder_1_out));  // open: cin, cout
  Multiplexer #(.width(32)) multiplexer_5 (
    .in0(adder_1_out), .in1(decoder_1_target), .out(target), .sel(ctrl_2[6]));  // open: en
  Multiplexer #(.width(32)) multiplexer_6 (.in0(A_t), .in1(plus_4_out), .out(A), .sel(ctrl_2[12]));  // open: en
  Add4 plus_4 (.In(PC_4), .Out(plus_4_out));

  assign PC_4out = PC_4;

  // Other names for the same wires on the sheet: ALUOp[3:0] = ctrl_2[4:1]; wb_t = ctrl[8]; Jump = ctrl_2[6];
  //   BranchOut = ctrl_2[7]; WBOut = ctrl_2[8]; Link = ctrl_2[12]; sign = ctrl_2[13]; MoveIn = ctrl_2[14];
  //   wb_dest[4:0] = ctrl[19:15]
endmodule

module Decoder (
  input  [31:0] ins,
  input  [31:0] PC_4,
  output [4:0] rs,
  output [4:0] rt,
  output [15:0] imm,
  output [31:0] ctrl,
  output [31:0] target
);

  ROM #(.addrWidth(12), .dataWidth(15)) rom_1 (.addr({ins[31:26], ins[5:0]}), .data(ctrl[14:0]));  // open: sel
  Multiplexer #(.width(5), .enable("false")) multiplexer_1 (
    .in0(ins[20:16]), .in1(ins[15:11]), .out(ctrl[19:15]), .sel(ctrl[5]));

  assign ctrl[31:20] = {{7{1'b0}}, ins[25:21]};
  assign imm = ins[31:16];
  assign rs = ins[10:6];
  assign rt = ins[15:11];
  assign target = {PC_4[31:28], ins[31:6], 2'b00};

  // Other names for the same wires on the sheet: op[5:0] = ins[5:0]; funct[5:0] = ins[31:26];
  //   j_target[25:0] = ins[31:6]; shamt[4:0] = ins[25:21]; rd[4:0] = ins[20:16]

  // Notes on the sheet:
  //   contents of rom_1 (hex, n*v repeats v):
  //   1280 0 1288 128a 1080 0 1088 108a 131f 31f 1281 1283 21*0 1284 0 128c 1290 1294 1298 129c 0 0 1297
  //   1299 20*0 1335 63*0 135f 63*0 35f 63*0 1321 63*0 1323 63*0 133e 63*0 133a 127*0 32a4 63*0 12b7 63*0
  //   12b9 63*0 12b0 63*0 12b4 63*0 12b8 63*0 12b1 1087*0 36a4 191*0 16a4 63*0 16a4 255*0 1ba4 191*0 1ba4
endmodule

module Our_ALU (
  input  [31:0] A,
  input  [31:0] B,
  input  [3:0] op,
  output [31:0] D
);

  wire comparator_1_lt, comparator_2_lt, multiplexer_1_out;
  wire [31:0] bit_extender_1_out, multiplexer_2_out;

  Comparator #(.width(32), .mode("unsigned")) comparator_1 (.a(A), .b(B), .lt(comparator_1_lt));  // open: gt, eq
  Comparator #(.width(32)) comparator_2 (.a(A), .b(B), .lt(comparator_2_lt));  // open: gt, eq
  Multiplexer #(.enable("false")) multiplexer_1 (
    .in0(comparator_1_lt), .in1(comparator_2_lt), .out(multiplexer_1_out), .sel(op[1]));
  assign bit_extender_1_out = {{31{1'b0}}, multiplexer_1_out};  // Bit_Extender bit_extender_1
  Multiplexer #(.width(32)) multiplexer_2 (
    .in0(bit_extender_1_out), .in1({A[15:0], {16{1'b0}}}), .out(multiplexer_2_out), .sel(op[2]));  // open: en
  Multiplexer #(.width(32)) multiplexer_3 (.in0(multiplexer_2_out), .in1(A), .out(D), .sel(op[3]));  // open: en
endmodule

module DataHazardBasic (
  input  [4:0] data,
  input  [4:0] dest,
  input  WE,
  output hazard
);

  wire comparator_1_eq, comparator_2_eq, not_1_out;

  Comparator #(.width(5)) comparator_1 (.a(data), .b(dest), .eq(comparator_1_eq));  // open: gt, lt
  Comparator #(.width(5)) comparator_2 (.a(dest), .b({5{1'b0}}), .eq(comparator_2_eq));  // open: gt, lt
  not not_1 (not_1_out, comparator_2_eq);
  and and_1 (hazard, comparator_1_eq, not_1_out, WE);
endmodule

module ForwarderBasic (
  input  [31:0] InputData,
  input  [31:0] ForwardedData,
  input  [4:0] InputRegister,
  input  [31:0] ctrl,
  output [31:0] CorrectData,
  output Hazard
);

  wire not_1_out;

  not not_1 (not_1_out, ctrl[8]);
  DataHazardBasic datahazardbasic_1 (.data(InputRegister), .dest(ctrl[19:15]), .WE(not_1_out), .hazard(Hazard));
  Multiplexer #(.width(32)) multiplexer_1 (
    .in0(InputData), .in1(ForwardedData), .out(CorrectData), .sel(Hazard));  // open: en
endmodule

module Forwarder (
  input  [31:0] InputData,
  input  [4:0] InputReg,
  input  [31:0] ForwardEX,
  input  [31:0] ForwardMEM,
  input  [31:0] ctrl_ex_out,
  input  [31:0] ctrl_mem_out,
  output [31:0] CorrectData
);

  wire EX_hazard;
  wire [31:0] EX_correctdata, MEM_correctdata;

  ForwarderBasic EX (
    .InputData(InputData), .ForwardedData(ForwardEX), .InputRegister(InputReg), .ctrl(ctrl_ex_out),
    .CorrectData(EX_correctdata), .Hazard(EX_hazard));
  ForwarderBasic MEM (
    .InputData(InputData), .ForwardedData(ForwardMEM), .InputRegister(InputReg), .ctrl(ctrl_mem_out),
    .CorrectData(MEM_correctdata));  // open: Hazard
  Multiplexer #(.width(32), .enable("false")) multiplexer_1 (
    .in0(MEM_correctdata), .in1(EX_correctdata), .out(CorrectData), .sel(EX_hazard));
endmodule

module LoadUseHazard (
  input  [4:0] InputRegister,
  input  [31:0] ctrl,
  output Hazard
);

  DataHazardBasic datahazardbasic_1 (.data(InputRegister), .dest(ctrl[19:15]), .WE(ctrl[9]), .hazard(Hazard));
endmodule

module Add4 (
  input  [31:0] In,
  output [31:0] Out
);

  // Incrementer incrementer_1: pin names not known; wires that end beside it: In[31:2], Out[31:2]

  assign Out[1:0] = 2'b00;
endmodule
